# Fritzing sketch electric_schema (saved by Fritzing 0.9.6b)
breadboards: 1

parts:
  Mod1 = Heltec WiFi LoRa 32 V2 [part_number=HTIT-WB32LA]
  Part1 = Color Sensor Breakout ADJD-S311
  Part2 = Color Sensor Breakout ADJD-S311
  U2 = GAS_SENSOR [package=mq-3]
  U3 = GAS_SENSOR [package=mq-3]
  M1 = DC Motor
  M2 = DC Motor
  Q1 = NPN-Transistor [package="SOT-23 [SMD]"]
  Q2 = NPN-Transistor [package="SOT-23 [SMD]"]
  HLK-PM1 = HLK-PM01

nets:
  N1: Mod1.pin_7, Q1.0
  N2: Mod1.pin_12, U2.B1
  N3: Mod1.pin_15, U3.B1
  N4: Mod1.pin_16, Mod1.pin_17
  GND: Mod1.GND, Part1.GND, Part2.GND, U2.H1, M1.pin_1, M2.pin_1, HLK-PM1.-Vo
  N5: Mod1.pin_21, Mod1.pin_22
  N6: Mod1.pin_27, Q2.0
  N7: Mod1.pin_32, Part2.SDA
  N8: Mod1.pin_34, Part2.SCL
  N9: Mod1.pin_35, Part1.SDA
  N10: Mod1.pin_36, Part1.SCL
  VCC: Part1.VCC, Part2.VCC, U2.H2, U3.H2, Q1.1, Q2.1, HLK-PM1.+Vo
  N11: M1.pin_2, Q2.2
  N12: M2.pin_2, Q1.2
